# Fritzing sketch debogage_sortie_analogique (saved by Fritzing 0.9.3b)
breadboards: 1

parts:
  Composant1 = Arduino Nano (Rev3.0)
  R1 = Resistor [tolerance=±5% resistance=100 package=THT]
  LED1 = LED - 5mm [color="Red (633nm)" package="5 mm [THT]"]

nets:
  GND: Composant1.GND, R1.Pin_0
  N1: Composant1.D9, LED1.anode
  N2: R1.Pin_1, LED1.cathode
