# Fritzing sketch alimenter_del_circuit (saved by Fritzing 0.9.3b)
breadboards: 1

parts:
  Composant1 = Arduino Nano (Rev3.0)
  R1 = Resistor [tolerance=±5% resistance=100 package=THT]
  LED1 = LED - 5mm [color="Red (633nm)" package="5 mm [THT]"]

nets:
  GND: Composant1.GND, LED1.cathode
  5V: Composant1.5V, R1.Pin_1
  N1: R1.Pin_0, LED1.anode
