# Fritzing sketch Allumer une DEL (saved by Fritzing 0.9.3b)
breadboards: 1

parts:
  Composant1 = Arduino Nano (Rev3.0) (ICSP)
  LED1 = smd LED [color="Red (633nm)" package="0603 [SMD]"]
  R1 = Resistor [tolerance=±5% resistance=100 package="1206 [SMD]"]

nets:
  N1: Composant1.GND, R1.Pin_0
  N2: Composant1.D3, LED1.anode
  N3: LED1.cathode, R1.Pin_1
