# Fritzing sketch del_arduino (saved by Fritzing 0.9.3b)
breadboards: 1

parts:
  R3 = Resistor [tolerance=±5% resistance=200 package=THT]
  LED1 = LED - 5mm [color="Orange (620nm)" package="5 mm [THT]"]
  Composant1 = Arduino Nano (Rev3.0) (ICSP)

nets:
  N1: R3.Pin_0, Composant1.D5
  N2: R3.Pin_1, LED1.anode
  GND: LED1.cathode, Composant1.GND
  5V: Composant1.5V
