# Fritzing sketch exemple_osc_final (saved by Fritzing 0.9.3b)
breadboards: 1

parts:
  R3 = Resistor [tolerance=±5% resistance=200 package=THT]
  LED1 = LED - 5mm [color="Orange (620nm)" package="5 mm [THT]"]
  R2 = Photocell (LDR) [package=THT]
  R4 = Resistor [tolerance=±5% resistance=100k package=THT]
  BUTTON2 = Arcade Button (red)
  LED2 = LED - 5mm [color="Red (633nm)" package="5 mm [THT]"]
  R5 = Resistor [tolerance=±5% resistance=200 package=THT]
  Composant1 = Arduino Nano (Rev3.0) (ICSP)
  U3 = POT [package=pot_alpha_rv16af-20]

nets:
  N1: R3.Pin_0, Composant1.D5
  N2: R3.Pin_1, LED1.anode
  GND: LED1.cathode, R2.pin_0, BUTTON2.no_name_yet#1, LED2.cathode, Composant1.GND, U3.E
  N3: R2.pin_1, R4.Pin_1, Composant1.A1
  5V: R4.Pin_0, Composant1.5V, U3.A
  N4: BUTTON2.no_name_yet#2, Composant1.D2
  N5: LED2.anode, R5.Pin_1
  N6: R5.Pin_0, Composant1.D3
  N7: Composant1.A0, U3.S

custom parts:
  Arcade Button (red): Adafruit Arcade Button (red)
