# Fritzing sketch bouton_arcade_photocell_potentiometre (saved by Fritzing 0.9.3b)
breadboards: 1

parts:
  LED2 = LED - 5mm [color="Red (633nm)" package="5 mm [THT]"]
  part = Resistor [tolerance=±5% resistance=200 package=THT]
  Composant1 = Arduino Nano (Rev3.0) (ICSP)
  S1 = Pushbutton [package="[THT]"]
  LED1 = LED - 5mm [color="Red (633nm)" package="5 mm [THT]"]
  U1 = POT [package=pot_mammoth]
  R2 = Photocell (LDR) [package=THT]
  part_2 = Resistor [tolerance=±5% resistance=100k package=THT]

nets:
  N1: LED2.cathode, LED1.anode
  N2: LED2.anode, part.Pin_0
  N3: part.Pin_1, Composant1.D3
  GND: Composant1.GND, S1.Pin_1, S1.Pin_2, LED1.cathode, U1.A, R2.pin_1
  N4: Composant1.D2, S1.Pin_3, S1.Pin_4
  5V: Composant1.5V, U1.E, part_2.Pin_0
  N5: Composant1.A1, R2.pin_0, part_2.Pin_1
  N6: Composant1.A0, U1.S
